# Fritzing sketch MiniGolfer (saved by Fritzing 1.0.1rc)
breadboards: 1

parts:
  Raspberry_Pi_1 = Raspberry Pi 3 [part_number=RPI-3-V1.2]
  Adafruit_OV5640_Camera_Breakout1 = Adafruit OV5640 Camera Breakout [part_number=#5673]  # not connected
  BATT1 = 4xAA Switchable Battery Pack w/Bare Wire
  BATT2 = 4xAA Switchable Battery Pack w/Bare Wire
  HC-SR04_Sensor_1 = HC-SR04 Ultrasonic Distance Sensor  # not connected
  HC-SR04_Sensor_2 = HC-SR04 Ultrasonic Distance Sensor  # not connected
  S1 = H-Bridge with L298N
  M1 = DC Mini Metal Gear Motor
  M2 = DC Mini Metal Gear Motor
  M3 = DC Mini Metal Gear Motor  # not connected
  U2 = LIPO-2000mAh [package=lipo-2000]  # not connected

nets:
  GND: Raspberry_Pi_1.GND, BATT1.NEG, S1.GND
  N1: BATT1.POS, BATT2.NEG
  N2: BATT2.POS, S1.12V
  N3: S1.M1-01, M2.IN2
  N4: S1.M1-02, M2.IN1
  N5: S1.M2-01, M1.IN2
  N6: S1.M2-02, M1.IN1

custom parts:
  Adafruit OV5640 Camera Breakout: Hobby-level microcontrollers are finally getting big and powerful enough to start handling camera modules that historically would have required a full computer or FPGA to handle. The RP2040 and ESP32-Sx series of chips, for example, have enough pins to communicate with the 8-bit data output, DMA to quickly grab a frame, and the necessary RAM to buffer a raw snapshot. Now all we need is a nice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
  4xAA Switchable Battery Pack w/Bare Wire: 4xAA Switchable Battery Pack with Bare Wire connection
  H-Bridge with L298N: h-bridge
